# Fritzing sketch Schema (saved by Fritzing 0.9.3b)

parts:
  DHT11 = DHT11 Humitidy and Temperature Sensor
  Raspberry_Pi = Raspberry Pi 3 [part_number=RPI-3-V1.2]

nets:
  VDD: DHT11.VDD, Raspberry_Pi.5V
  N1: DHT11.DATA, Raspberry_Pi.GIPO4
  GND: DHT11.GND, Raspberry_Pi.GND

custom parts:
  DHT11 Humitidy and Temperature Sensor: DHT11 Humidity and Temperature Sensor
